# Fritzing sketch Schaltplan_Temperature (saved by Fritzing 0.6.3b)
breadboards: 1

parts:
  T1 = LM34 Temperature Sensor [package="TO92 [THT]"]
  Arduino1 = Arduino
  R1 = Resistor [tolerance=±5% resistance=4.7k package="0603 [SMD]"]

nets:
  GND: T1.+Vs, T1.GND, Arduino1.GND
  N1: T1.Vout, Arduino1.D10, R1.Pin_1
  N2: Arduino1.+5V, R1.Pin_0
